# Fritzing sketch leonardo3v2 (saved by Fritzing 0.9.3b)
breadboards: 6

parts:
  Raspberry_Pi_1 = Raspberry Pi 3 [part_number=RPI-3-V1.2]
  F1 = FUSE [package=fuse_5mm]
  F2 = FUSE [package=fuse_5mm]
  VCC3 = Battery block 9V
  M13 = DC Motor
  M14 = DC Motor
  M15 = DC Motor
  M16 = DC Motor
  Componente12 = MD10C
  Componente13 = Motor Driver 1A Dual TB6612FNG
  Componente14 = Motor Driver 1A Dual TB6612FNG
  M17 = DC Motor
  M18 = DC Motor
  Componente15 = MD10C
  M19 = DC Motor
  Componente16 = MD10C
  Componente18 = SRF05 Ultrasonic Rangefinder
  Componente19 = SRF05 Ultrasonic Rangefinder
  Componente20 = SRF05 Ultrasonic Rangefinder
  R2 = Resistor [tolerance=±5% resistance=220 package=THT]
  R3 = Resistor [tolerance=±5% resistance=220 package=THT]
  R4 = Resistor [tolerance=±5% resistance=220 package=THT]
  R5 = Resistor [tolerance=±5% resistance=220 package=THT]
  R6 = Resistor [tolerance=±5% resistance=220 package=THT]
  R7 = Resistor [tolerance=±5% resistance=220 package=THT]
  R8 = Resistor [tolerance=±5% resistance=220 package=THT]
  R9 = Resistor [tolerance=±5% resistance=220 package=THT]
  R10 = Resistor [tolerance=±5% resistance=220 package=THT]
  F3 = FUSE [package=fuse_5mm]

nets:
  N1: Raspberry_Pi_1.GPIO2, R5.Pin_0, R6.Pin_1
  N2: Raspberry_Pi_1.GPIO3, Componente20.Trig
  N3: Raspberry_Pi_1.GIPO4, R2.Pin_0, R4.Pin_1
  GND: Raspberry_Pi_1.GND, VCC3.-, Componente12.GND, Componente13.GND, Componente14.GND, Componente15.GND, Componente16.GND, Componente18.GND, Componente19.GND, Componente20.GND, R7.Pin_1, R10.Pin_1
  N4: Raspberry_Pi_1.GIPO17, Componente19.Trig
  N5: Raspberry_Pi_1.GIPO27, R8.Pin_0, R9.Pin_1
  N6: Raspberry_Pi_1.GIPO22, Componente18.Trig
  N7: Raspberry_Pi_1.GIPO10, Componente15.PWMB
  N8: Raspberry_Pi_1.GIPO9, Componente16.DIRB
  N9: Raspberry_Pi_1.GIPO11, Componente16.PWMB
  N10: Raspberry_Pi_1.GIPO5, Componente14.AIN1
  N11: Raspberry_Pi_1.GIPO6, Componente14.AIN2
  N12: Raspberry_Pi_1.GIPO13, Componente14.PWMA
  N13: Raspberry_Pi_1.GIPO19, Componente14.PWMB
  N14: Raspberry_Pi_1.GIPO26, Componente14.BIN2
  N15: Raspberry_Pi_1.GIPO21, Componente14.BIN1
  N16: Raspberry_Pi_1.GIPO20, Componente13.AIN1
  N17: Raspberry_Pi_1.GIPO16, Componente13.AIN2
  N18: Raspberry_Pi_1.GIPO12, Componente13.PWMA
  N19: Raspberry_Pi_1.GIPO7, Componente14.STBY
  N20: Raspberry_Pi_1.GIPO8, Componente13.STBY
  N21: Raspberry_Pi_1.GIPO25, Componente12.DIRB
  N22: Raspberry_Pi_1.GIPO24, Componente12.PWMB
  N23: Raspberry_Pi_1.GIPO23, Componente15.DIRB
  N24: Raspberry_Pi_1.GIPO18, Componente13.PWMB
  N25: Raspberry_Pi_1.GIPO15, Componente13.BIN2
  N26: Raspberry_Pi_1.GIPO14, Componente13.BIN1
  N27: Raspberry_Pi_1.5V, F1.1, F3.1
  VCC: F1.2, Componente13.VCC, Componente14.VCC
  N28: F2.1, VCC3.+
  N29: F2.2, Componente12.VM, Componente13.VM, Componente14.VM, Componente15.VM, Componente16.VM
  N30: M13.pin_1, Componente13.B01
  N31: M13.pin_2, Componente13.B02
  N32: M14.pin_1, Componente13.A02
  N33: M14.pin_2, Componente13.A01
  N34: M15.pin_1, Componente14.B01
  N35: M15.pin_2, Componente14.B02
  N36: M16.pin_1, Componente14.A02
  N37: M16.pin_2, Componente14.A01
  N38: Componente12.B01, M17.pin_2
  N39: Componente12.B02, M17.pin_1
  N40: M18.pin_1, Componente15.B02
  N41: M18.pin_2, Componente15.B01
  N42: M19.pin_1, Componente16.B02
  N43: M19.pin_2, Componente16.B01
  VCC_2: Componente18.VCC, Componente19.VCC, Componente20.VCC, F3.2
  N44: Componente18.Echo, R9.Pin_0
  N45: Componente19.Echo, R4.Pin_0
  N46: Componente20.Echo, R6.Pin_0
  N47: R2.Pin_1, R3.Pin_0
  N48: R5.Pin_1, R7.Pin_0
  N49: R8.Pin_1, R10.Pin_0

notes:
  MOTORI MOVIMENTO
  Cavi rosa giallo verde e blu: direzione motori movimento
  Cavo arancio: pin trig sensore
  Cavo bianco: pin echo sensore
  Cavo grigio: segnale pwm
  MOTORI ALZARE E ABBASSARE
  Cavo viola: segnale stand-by
  Cavo marrone: direzione motori sollevamento
  12 VOLT
  Cavi ocra e ciano: pin motori
  Resistori partitori di tensione: 3 uguali a resistenza diverse

custom parts:
  MD10C: The TB6612FNG motor driver can control up to two DC motors at a constant current of 1.2A (3.2A peak). Two input signals (IN1 and IN2) can be used to control the motor in one of four function modes - CW, CCW, short-brake, and stop. The two motor outputs (A and B) can be separately controlled, the speed of each motor is controlled via a PWM input signal with a frequency up to 100kHz. The STBY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
  Motor Driver 1A Dual TB6612FNG: The TB6612FNG motor driver can control up to two DC motors at a constant current of 1.2A (3.2A peak). Two input signals (IN1 and IN2) can be used to control the motor in one of four function modes - CW, CCW, short-brake, and stop. The two motor outputs (A and B) can be separately controlled, the speed of each motor is controlled via a PWM input signal with a frequency up to 100kHz. The STBY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
