# Fritzing sketch leonardo4v2 (saved by Fritzing 0.9.3b)
breadboards: 8

parts:
  Raspberry_Pi_1 = Raspberry Pi 3 [part_number=RPI-3-V1.2]
  F1 = FUSE [package=fuse_5mm]
  F2 = FUSE [package=fuse_5mm]
  VCC3 = Battery block 9V
  M13 = DC Motor
  M14 = DC Motor
  M15 = DC Motor
  M16 = DC Motor
  Componente12 = MD10C
  Componente13 = Motor Driver 1A Dual TB6612FNG
  Componente14 = Motor Driver 1A Dual TB6612FNG
  M17 = DC Motor
  M18 = DC Motor
  Componente15 = MD10C
  M19 = DC Motor
  Componente16 = MD10C
  Componente18 = SRF05 Ultrasonic Rangefinder
  Componente19 = SRF05 Ultrasonic Rangefinder
  Componente20 = SRF05 Ultrasonic Rangefinder
  R2 = Resistor [tolerance=±5% resistance=220 package=THT]
  R3 = Resistor [tolerance=±5% resistance=220 package=THT]
  R4 = Resistor [tolerance=±5% resistance=220 package=THT]
  R5 = Resistor [tolerance=±5% resistance=220 package=THT]
  R6 = Resistor [tolerance=±5% resistance=220 package=THT]
  R7 = Resistor [tolerance=±5% resistance=220 package=THT]
  R8 = Resistor [tolerance=±5% resistance=220 package=THT]
  R9 = Resistor [tolerance=±5% resistance=220 package=THT]
  R10 = Resistor [tolerance=±5% resistance=220 package=THT]
  F3 = FUSE [package=fuse_5mm]
  U1 = MCP23017 [package=dil28-3]

nets:
  N1: Raspberry_Pi_1.GPIO2, U1.SDA
  N2: Raspberry_Pi_1.GPIO3, U1.SCL
  N3: Raspberry_Pi_1.GIPO4, U1.RESET
  GND: Raspberry_Pi_1.GND, VCC3.-, Componente12.GND, Componente13.GND, Componente14.GND, Componente15.GND, Componente16.GND, Componente18.GND, Componente19.GND, Componente20.GND, R3.Pin_1, R7.Pin_1, R10.Pin_1, U1.GND, U1.A0, U1.A1, U1.A2
  N4: Raspberry_Pi_1.GIPO17, Componente13.PWMB
  N5: Raspberry_Pi_1.GIPO27, Componente13.PWMA
  N6: Raspberry_Pi_1.GIPO19, R5.Pin_0, R6.Pin_1
  N7: Raspberry_Pi_1.GIPO26, Componente20.Trig
  N8: Raspberry_Pi_1.GIPO21, R2.Pin_0, R4.Pin_1
  N9: Raspberry_Pi_1.GIPO20, Componente19.Trig
  N10: Raspberry_Pi_1.GIPO16, R8.Pin_0, R9.Pin_1
  N11: Raspberry_Pi_1.GIPO12, Componente18.Trig
  N12: Raspberry_Pi_1.GIPO7, Componente12.DIRB
  N13: Raspberry_Pi_1.GIPO8, Componente12.PWMB
  N14: Raspberry_Pi_1.GIPO25, Componente15.DIRB
  N15: Raspberry_Pi_1.GIPO24, Componente15.PWMB
  N16: Raspberry_Pi_1.GIPO23, Componente16.DIRB
  N17: Raspberry_Pi_1.GIPO18, Componente16.PWMB
  N18: Raspberry_Pi_1.GIPO15, Componente14.PWMB
  N19: Raspberry_Pi_1.GIPO14, Componente14.PWMA
  N20: Raspberry_Pi_1.5V, F1.1, F3.1
  VCC: F1.2, Componente18.VCC, Componente19.VCC, Componente20.VCC
  N21: F2.1, VCC3.+
  N22: F2.2, Componente12.VM, Componente13.VM, Componente14.VM, Componente15.VM, Componente16.VM
  N23: M13.pin_1, Componente13.B01
  N24: M13.pin_2, Componente13.B02
  N25: M14.pin_1, Componente13.A02
  N26: M14.pin_2, Componente13.A01
  N27: M15.pin_1, Componente14.B01
  N28: M15.pin_2, Componente14.B02
  N29: M16.pin_1, Componente14.A02
  N30: M16.pin_2, Componente14.A01
  N31: Componente12.B01, M17.pin_2
  N32: Componente12.B02, M17.pin_1
  VCC_2: Componente13.VCC, Componente14.VCC, F3.2, U1.VCC
  N33: Componente13.AIN1, U1.GPB1
  N34: Componente13.AIN2, U1.GPB0
  N35: Componente13.STBY, U1.GPB2
  N36: Componente13.BIN1, U1.GPB3
  N37: Componente13.BIN2, U1.GPB4
  N38: Componente14.AIN1, U1.GPA4
  N39: Componente14.AIN2, U1.GPA3
  N40: Componente14.STBY, U1.GPA5
  N41: Componente14.BIN1, U1.GPA6
  N42: Componente14.BIN2, U1.GPA7
  N43: M18.pin_1, Componente15.B02
  N44: M18.pin_2, Componente15.B01
  N45: M19.pin_1, Componente16.B02
  N46: M19.pin_2, Componente16.B01
  N47: Componente18.Echo, R9.Pin_0
  N48: Componente19.Echo, R4.Pin_0
  N49: Componente20.Echo, R6.Pin_0
  N50: R2.Pin_1, R3.Pin_0
  N51: R5.Pin_1, R7.Pin_0
  N52: R8.Pin_1, R10.Pin_0

notes:
  MOTORI MOVIMENTO
  Cavi rosa giallo verde e blu: direzione motori movimento
  Cavo arancio: pin trig sensore
  Cavo bianco: pin echo sensore
  Cavo grigio: segnale pwm
  MOTORI SOLLEVAMENTO (SOSTITUIRE CON STEPPER)
  Cavo viola: segnale stand-by
  Cavo marrone: direzione motori sollevamento
  12 VOLT
  Cavi ciano: pin interfaccia I2C
  Resistori partitori di tensione: 3 uguali a resistenza diverse

custom parts:
  MD10C: The TB6612FNG motor driver can control up to two DC motors at a constant current of 1.2A (3.2A peak). Two input signals (IN1 and IN2) can be used to control the motor in one of four function modes - CW, CCW, short-brake, and stop. The two motor outputs (A and B) can be separately controlled, the speed of each motor is controlled via a PWM input signal with a frequency up to 100kHz. The STBY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
  Motor Driver 1A Dual TB6612FNG: The TB6612FNG motor driver can control up to two DC motors at a constant current of 1.2A (3.2A peak). Two input signals (IN1 and IN2) can be used to control the motor in one of four function modes - CW, CCW, short-brake, and stop. The two motor outputs (A and B) can be separately controlled, the speed of each motor is controlled via a PWM input signal with a frequency up to 100kHz. The STBY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
  MCP23017: 16 bit I/O chip controlled via I2C
